// Logisim project proj_2_1.circ as structural Verilog: 7 circuits, main circuit testbench
module inst_fetch (
  input  clk,
  input  rst,
  input  control_en_i,
  input  [31:0] control_pc_i,
  input  [15:0] inst_i,
  output inst_en_o,
  output [31:0] current_pc_o,
  output [31:0] inst_addr_o,
  output [15:0] inst_o
);

  wire not_1_out, not_2_out;
  wire [31:0] adder_1_out, counter_1_q, multiplexer_1_out;

  not not_1 (not_1_out, rst);
  Adder #(.width(32)) adder_1 (.a(control_pc_i), .b(32'h1), .out(adder_1_out));  // open: cin, cout
  Counter #(.max('hffffffff), .width(32)) counter_1 (
    .clr(rst), .load(control_en_i), .up(not_1_out), .count(not_1_out), .clk(clk), .D(adder_1_out),
    .Q(counter_1_q));  // open: carry
  Multiplexer #(.width(32)) multiplexer_1 (
    .in0(counter_1_q), .in1(control_pc_i), .out(multiplexer_1_out), .sel(control_en_i));
  not not_2 (not_2_out, rst);
  Register #(.width(32)) register_1 (.D(multiplexer_1_out), .en(not_2_out), .clk(clk), .Q(current_pc_o), .clr(rst));
  not not_3 (inst_en_o, rst);

  assign inst_addr_o = current_pc_o;
  assign inst_o = inst_i;

  // Notes on the sheet:
  //   Don't touch
endmodule

module TOP (
  input  rst,
  input  clk,
  input  [15:0] inst,
  input  [31:0] mem_result,
  input  [31:0] current_pc,
  output mem_wen,
  output [31:0] mem_din,
  output mem_ren,
  output [31:0] alu_result,
  output control_en,
  output [31:0] control_pc,
  output wb_en,
  output [4:0] wb_addr,
  output [31:0] wb_data
);

  wire [4:0] li_1_address, lui_1_address, multiplexer_1_out;
  wire [31:0] adder_1_out, li_2_imm, lui_2_imm, multiplexer_2_out;

  Register #(.width(32)) register_1 (.D(adder_1_out), .clk(clk), .Q(control_pc), .clr(rst));  // open: en
  Adder #(.width(32)) adder_1 (.a(current_pc), .b(32'h1), .out(adder_1_out));  // open: cin, cout
  li li_1 (.inst_i(inst), .address(li_1_address));  // open: imm
  lui lui_1 (.inst_i(inst), .address(lui_1_address));  // open: imm
  li li_2 (.inst_i(inst), .imm(li_2_imm));  // open: address
  lui lui_2 (.inst_i(inst), .imm(lui_2_imm));  // open: address
  Multiplexer #(.select(5), .width(5)) multiplexer_1 (
    .in10(li_1_address), .in11(lui_1_address), .out(multiplexer_1_out), .sel({inst[1:0], inst[15:13]}));  // open: in0, in1, in2, in3, in4, in5, in6, in7, in8, in9, in12, in13, in14, in15, in16, in17, in18, in19, in20, in21, in22, in23, in24, in25, in26, in27, in28, in29, in30, in31
  Register #(.width(5)) register_2 (.D(multiplexer_1_out), .clk(clk), .Q(wb_addr));  // open: en, clr
  Register #(.width(32)) register_3 (.D(multiplexer_2_out), .clk(clk), .Q(alu_result));  // open: en, clr
  Multiplexer #(.select(5), .width(32)) multiplexer_2 (
    .in10(li_2_imm), .in11(lui_2_imm), .out(multiplexer_2_out), .sel({inst[1:0], inst[15:13]}));  // open: in0, in1, in2, in3, in4, in5, in6, in7, in8, in9, in12, in13, in14, in15, in16, in17, in18, in19, in20, in21, in22, in23, in24, in25, in26, in27, in28, in29, in30, in31

  assign control_en = 1'b0;
  assign mem_din = {32{1'b0}};
  assign mem_ren = 1'b0;
  assign mem_wen = 1'b0;
  assign wb_data = alu_result;
  assign wb_en = 1'b1;

  // Other names for the same wires on the sheet: FUNC3[2:0] = inst[15:13];
  //   select_type[4:0] = {inst[1:0], inst[15:13]}; OP[1:0] = inst[1:0]

  // Notes on the sheet:
  //   Fixed I/O
  //   Don't touch
endmodule

module testbench (
  input  rst,
  output mem_wen,
  output [31:0] mem_din,
  output mem_ren,
  output [31:0] alu_result,
  output control_en,
  output [31:0] control_pc,
  output halt,
  output wb_en,
  output [4:0] wb_addr,
  output [31:0] wb_data
);

  wire clk, inst_en, not_1_out, not_2_out, not_3_out, not_4_out, por_1_out, rst_t;
  wire [15:0] inst, inst_i;
  wire [31:0] current_pc, inst_addr, mem_result;

  not not_1 (not_1_out, inst_i[0]);
  not not_2 (not_2_out, inst_i[1]);
  not not_3 (not_3_out, inst_i[13]);
  not not_4 (not_4_out, inst_i[14]);
  and and_1 (halt, not_1_out, not_2_out, not_3_out, not_4_out, inst_i[15]);
  Clock clock_1 (.out(clk));
  or or_1 (rst_t, rst, por_1_out);
  POR por_1 (.out(por_1_out));
  inst_fetch inst_fetch_1 (
    .clk(clk), .rst(rst_t), .control_en_i(control_en), .control_pc_i(control_pc), .inst_i(inst_i),
    .inst_en_o(inst_en), .current_pc_o(current_pc), .inst_addr_o(inst_addr), .inst_o(inst));
  TOP top_1 (
    .rst(rst_t), .clk(clk), .inst(inst), .mem_result(mem_result), .current_pc(current_pc), .mem_wen(mem_wen),
    .mem_din(mem_din), .mem_ren(mem_ren), .alu_result(alu_result), .control_en(control_en),
    .control_pc(control_pc), .wb_en(wb_en), .wb_addr(wb_addr), .wb_data(wb_data));
  ROM #(.dataWidth(16)) rom_1 (.addr(inst_addr[7:0]), .data(inst_i));
  RAM #(.addrWidth(16), .clearpin("true"), .dataWidth(32), .\type ("nonvolatile")) ram_1 (
    .addr(alu_result[15:0]), .we(mem_wen), .oe(mem_ren), .clk(clk), .din(mem_din), .dout(mem_result),
    .clr(rst_t));

  // Notes on the sheet:
  //   contents of rom_1 (hex, n*v repeats v):
  //   4425 6525 40e 942a 84a2 49d 8000 1 1
  //   you can write any instruction in
endmodule

module instruction (
  input  [15:0] in_1
);

  wire [4:0] multiplexer_1_out, multiplexer_2_out;
  wire [31:0] alu_result;

  Multiplexer #(.select(3), .width(5)) multiplexer_1 (
    .in2(in_1[11:7]), .out(multiplexer_1_out));  // open: in0, in1, in3, in4, in5, in6, in7, sel
  Multiplexer #(.select(2), .width(5)) multiplexer_2 (
    .in1(multiplexer_1_out), .out(multiplexer_2_out), .sel(2'b11));  // open: in0, in2, in3
  assign alu_result = {{27{1'b0}}, multiplexer_2_out};  // Bit_Extender bit_extender_1

  // Other names for the same wires on the sheet: inst_i[15:0] = in_1; OP[1:0] = in_1[1:0];
  //   imm_CI[5:0] = {in_1[12], in_1[6:2]}; RS1_CI_CR[4:0] = in_1[11:7]; FUNC3[2:0] = in_1[15:13]
endmodule

module li (
  input  [15:0] inst_i,
  output [31:0] imm,
  output [4:0] address
);

  assign imm = {{26{1'b0}}, {inst_i[12], inst_i[6:2]}};  // Bit_Extender bit_extender_1

  assign address = inst_i[11:7];

  // Other names for the same wires on the sheet: imm_CI[5:0] = {inst_i[12], inst_i[6:2]}; RS1_CI[4:0] = inst_i[11:7]
endmodule

module Regfile (
  input  [4:0] register_i,
  input  [31:0] value,
  input  write,
  input  read,
  output [31:0] register_value
);

  wire clk;

  Clock clock_1 (.out(clk));
  RAM #(.addrWidth(5), .clearpin("true"), .dataWidth(32), .\type ("nonvolatile")) ram_1 (
    .addr(register_i), .we(write), .oe(read), .clk(clk), .din(value), .dout(register_value));  // open: clr
endmodule

module lui (
  input  [15:0] inst_i,
  output [31:0] imm,
  output [4:0] address
);

  wire [31:0] bit_extender_1_out;

  assign bit_extender_1_out = {{26{1'b0}}, {inst_i[12], inst_i[6:2]}};  // Bit_Extender bit_extender_1
  Shifter #(.width(32)) shifter_1 (.in(bit_extender_1_out), .\dist (5'b01100), .out(imm));

  assign address = inst_i[11:7];

  // Other names for the same wires on the sheet: imm_CI[5:0] = {inst_i[12], inst_i[6:2]}; RS1_CI[4:0] = inst_i[11:7]
endmodule
